// Logisim project LastUpdate.circ as structural Verilog: 1 circuit, main circuit main
// 3
module main (
  input  [3:0] in_1,
  input  [3:0] in_2,
  input  [3:0] in_3,
  input  [3:0] in_4
);

  wire and_2_out, and_3_out, and_4_out, and_5_out, and_6_out, and_7_out, and_8_out, and_9_out, and_10_out,
       and_11_out, and_12_out, and_13_out, and_14_out, and_15_out, and_16_out, and_17_out, and_18_out,
       and_19_out, and_21_out, and_22_out, and_23_out, and_24_out, and_25_out, and_26_out, and_27_out,
       and_28_out, and_29_out, and_30_out, and_31_out, and_32_out, and_33_out, and_34_out, and_35_out,
       and_36_out, bcd_to_7_segment_decoder_2_p3, BTNC_out, BTNL_out, BTNR_out, clock_1_out, comparator_1_eq,
       comparator_2_eq, comparator_3_eq, comparator_4_eq, d_ff_1_q, d_ff_2_q, d_ff_3_q, d_ff_4_q,
       decoder_1_out0, decoder_1_out1, decoder_1_out2, decoder_1_out3, decoder_2_out0, decoder_2_out1,
       decoder_2_out2, decoder_2_out3, Down_out, multiplexer_1_out, multiplexer_2_out, multiplexer_3_out,
       multiplexer_4_out, multiplexer_6_out, multiplexer_7_out, multiplexer_8_out, multiplexer_15_out,
       multiplexer_16_out, multiplexer_17_out, multiplexer_18_out, multiplexer_20_out, multiplexer_21_out,
       multiplexer_22_out, multiplexer_24_out, nor_2_out, nor_3_out, nor_4_out, nor_5_out, nor_6_out,
       nor_7_out, nor_8_out, nor_9_out, not_1_out, not_2_out, not_3_out, not_4_out, not_5_out, not_6_out,
       not_7_out, or_1_out, or_2_out, or_3_out, or_4_out, or_5_out, or_6_out, t_ff_1_q, t_ff_2_q, UP_out;
  wire [1:0] and_1_out, counter_10_q;
  wire [2:0] bcd_to_7_segment_decoder_2_p1, counter_1_q, counter_2_q, counter_3_q, counter_6_q, counter_8_q,
       counter_9_q, multiplexer_19_out;
  wire [3:0] bcd_to_7_segment_decoder_4_p3, bcd_to_7_segment_decoder_5_p1, bcd_to_7_segment_decoder_6_p1,
       bcd_to_7_segment_decoder_7_p1, bcd_to_7_segment_decoder_8_p1, bcd_to_7_segment_decoder_12_p1,
       counter_4_q, counter_5_q, counter_7_q, counter_11_q, counter_12_q, multiplexer_11_out, undriven;
  wire [5:0] counter_13_q;

  Button UP (.out(UP_out));
  Button Down (.out(Down_out));
  nor nor_1 (and_1_out[0], UP_out, Down_out);
  not not_1 (not_1_out, Down_out);
  and and_1 (and_1_out[1], UP_out, not_1_out);
  or or_1 (or_1_out, UP_out, Down_out);
  Clock clock_1 (.out(clock_1_out));
  Multiplexer #(.select(2)) multiplexer_1 (
    .in0(and_11_out), .in1(1'b0), .in2(or_4_out), .in3(1'b0), .out(multiplexer_1_out), .sel(and_1_out));
  and and_2 (and_2_out, nor_5_out, not_3_out);
  Multiplexer #(.select(2)) multiplexer_2 (
    .in0(and_2_out), .in1(or_5_out), .in2(1'b0), .in3(1'b0), .out(multiplexer_2_out),
    .sel({and_1_out[0], and_1_out[1]}));
  Multiplexer multiplexer_3 (.in0(and_7_out), .in1(1'b1), .out(multiplexer_3_out), .sel(and_28_out));
  or or_2 (or_2_out, and_9_out, and_3_out);
  Counter #(.max('h7), .width(3)) counter_1 (
    .clr(or_2_out), .up(and_1_out[1]), .count(decoder_2_out2), .clk(multiplexer_1_out), .Q(counter_1_q));  // open: load, D, carry
  Multiplexer multiplexer_4 (.in0(counter_4_q[3]), .in1(multiplexer_2_out), .out(multiplexer_4_out), .sel(and_28_out));
  Counter #(.max('h7), .width(3)) counter_2 (
    .clr(or_3_out), .up(multiplexer_8_out), .count(multiplexer_3_out), .clk(multiplexer_4_out),
    .Q(counter_2_q));  // open: load, D, carry
  _7_Segment_Display u_7_segment_display_1 ();  // open: g, f, a, b, e, d, c, dp
  // BCD_to_7_Segment_decoder bcd_to_7_segment_decoder_1: pin names not known; wires that end beside it: {1'b0, counter_1_q}, 1'b0
  _7_Segment_Display u_7_segment_display_2 ();  // open: g, f, a, b, e, d, c, dp
  // BCD_to_7_Segment_decoder bcd_to_7_segment_decoder_2: pin names not known; wires that end beside it: {1'b0, bcd_to_7_segment_decoder_2_p1}, 1'b0, bcd_to_7_segment_decoder_2_p3
  or or_3 (or_3_out, and_8_out, and_6_out);
  Counter #(.max('h7), .width(3)) counter_3 (
    .clr(counter_3_q[2]), .clk(clock_1_out), .Q(counter_3_q));  // open: load, up, count, D, carry
  and and_3 (and_3_out, counter_1_q[0], counter_1_q[1]);
  Counter #(.max('hf), .width(4)) counter_4 (
    .up(1'b1), .count(and_13_out), .clk(clock_1_out), .Q(counter_4_q));  // open: clr, load, D, carry
  and and_4 (and_4_out, Down_out, nor_5_out);
  Multiplexer #(.width(3)) multiplexer_5 (
    .in0(counter_2_q), .in1(counter_1_q), .out(bcd_to_7_segment_decoder_2_p1),
    .sel(bcd_to_7_segment_decoder_2_p3));
  and and_5 (and_5_out, nor_3_out, Down_out);
  Multiplexer multiplexer_6 (.in0(and_24_out), .in1(1'b1), .out(multiplexer_6_out), .sel(and_28_out));
  and and_6 (and_6_out, counter_2_q[0], counter_2_q[1]);
  and and_7 (and_7_out, and_24_out, and_16_out);
  Counter #(.max('hf), .width(4)) counter_5 (
    .clr(or_4_out), .load(and_5_out), .up(and_1_out[1]), .count(decoder_2_out2), .clk(or_1_out), .D(in_4),
    .Q(counter_5_q));  // open: carry
  Multiplexer multiplexer_7 (.in0(counter_4_q[3]), .in1(or_1_out), .out(multiplexer_7_out), .sel(and_28_out));
  Multiplexer multiplexer_8 (.in0(1'b1), .in1(and_1_out[1]), .out(multiplexer_8_out), .sel(and_28_out));
  Comparator #(.width(3)) comparator_1 (.a(counter_2_q), .b(counter_1_q), .eq(comparator_1_eq));  // open: gt, lt
  or or_4 (or_4_out, and_12_out, and_9_out);
  _7_Segment_Display u_7_segment_display_3 ();  // open: g, f, a, b, e, d, c, dp
  // BCD_to_7_Segment_decoder bcd_to_7_segment_decoder_3: pin names not known; wires that end beside it: counter_5_q
  and and_8 (and_8_out, counter_2_q[1], counter_7_q[2]);
  or or_5 (or_5_out, and_15_out, and_8_out);
  _7_Segment_Display u_7_segment_display_4 ();  // open: g, f, a, b, e, d, c, dp
  // BCD_to_7_Segment_decoder bcd_to_7_segment_decoder_4: pin names not known; wires that end beside it: counter_3_q, 4'b0000, bcd_to_7_segment_decoder_4_p3
  Multiplexer #(.width(4)) multiplexer_9 (
    .in0(undriven), .in1(multiplexer_11_out), .out(bcd_to_7_segment_decoder_4_p3), .sel(decoder_1_out3));
  and and_9 (and_9_out, counter_1_q[1], counter_5_q[2]);
  Counter #(.max('h7), .width(3)) counter_6 (
    .up(1'b1), .count(1'b1), .clk(clock_1_out), .Q(counter_6_q));  // open: clr, load, D, carry
  Counter #(.max('hf), .width(4)) counter_7 (
    .clr(or_5_out), .load(and_4_out), .up(multiplexer_8_out), .count(multiplexer_6_out),
    .clk(multiplexer_7_out), .D(in_1), .Q(counter_7_q));  // open: carry
  _7_Segment_Display u_7_segment_display_5 ();  // open: g, f, a, b, e, d, c, dp
  // BCD_to_7_Segment_decoder bcd_to_7_segment_decoder_5: pin names not known; wires that end beside it: bcd_to_7_segment_decoder_5_p1, bcd_to_7_segment_decoder_2_p3
  _7_Segment_Display u_7_segment_display_6 ();  // open: g, f, a, b, e, d, c, dp
  // BCD_to_7_Segment_decoder bcd_to_7_segment_decoder_6: pin names not known; wires that end beside it: bcd_to_7_segment_decoder_6_p1
  Multiplexer #(.width(4)) multiplexer_10 (
    .in0(undriven), .in1(multiplexer_11_out), .out(bcd_to_7_segment_decoder_6_p1), .sel(decoder_1_out2));
  Decoder #(.select(2)) decoder_1 (
    .out0(decoder_1_out0), .out1(decoder_1_out1), .out2(decoder_1_out2), .out3(decoder_1_out3),
    .sel(counter_3_q[1:0]), .en(1'b1));
  D_Flip_Flop d_ff_1 (.D(and_10_out), .clk(Down_out), .Q(d_ff_1_q));  // open: Qn, preset, reset
  and and_10 (and_10_out, counter_5_q[0], nor_2_out);
  nor nor_2 (nor_2_out, counter_5_q[2], counter_5_q[3], counter_5_q[2]);
  nor nor_3 (nor_3_out, counter_5_q[3], counter_5_q[0], counter_5_q[2], counter_5_q[1]);
  not not_2 (not_2_out, d_ff_1_q);
  and and_11 (and_11_out, nor_3_out, not_2_out);
  Multiplexer #(.select(2), .width(4)) multiplexer_11 (
    .in0(bcd_to_7_segment_decoder_12_p1), .in1({1'b0, multiplexer_19_out}),
    .in2(bcd_to_7_segment_decoder_5_p1), .in3({1'b0, bcd_to_7_segment_decoder_2_p1}),
    .out(multiplexer_11_out), .sel(counter_3_q[1:0]));
  and and_12 (and_12_out, counter_5_q[1], counter_5_q[3]);
  Multiplexer #(.width(4)) multiplexer_12 (
    .in0(counter_7_q), .in1(counter_5_q), .out(bcd_to_7_segment_decoder_5_p1),
    .sel(bcd_to_7_segment_decoder_2_p3));
  _7_Segment_Display u_7_segment_display_7 ();  // open: g, f, a, b, e, d, c, dp
  // BCD_to_7_Segment_decoder bcd_to_7_segment_decoder_7: pin names not known; wires that end beside it: bcd_to_7_segment_decoder_7_p1
  Multiplexer #(.width(4)) multiplexer_13 (
    .in0(undriven), .in1(multiplexer_11_out), .out(bcd_to_7_segment_decoder_7_p1), .sel(decoder_1_out1));
  and and_13 (and_13_out, counter_6_q[0], counter_6_q[1], counter_6_q[2]);
  and and_14 (and_14_out, counter_7_q[0], nor_4_out);
  nor nor_4 (nor_4_out, counter_7_q[1], counter_7_q[2], counter_7_q[3]);
  nor nor_5 (nor_5_out, counter_7_q[3], counter_7_q[0], counter_7_q[2], counter_7_q[1]);
  _7_Segment_Display u_7_segment_display_8 ();  // open: g, f, a, b, e, d, c, dp
  // BCD_to_7_Segment_decoder bcd_to_7_segment_decoder_8: pin names not known; wires that end beside it: bcd_to_7_segment_decoder_8_p1
  Multiplexer #(.width(4)) multiplexer_14 (
    .in0(undriven), .in1(multiplexer_11_out), .out(bcd_to_7_segment_decoder_8_p1), .sel(decoder_1_out0));
  Multiplexer #(.select(2)) multiplexer_15 (
    .in0(and_21_out), .in1(1'b0), .in2(and_29_out), .in3(1'b0), .out(multiplexer_15_out), .sel(and_1_out));
  Button BTNC (.out(BTNC_out));
  Button BTNR (.out(BTNR_out));
  Button BTNL (.out(BTNL_out));
  not not_3 (not_3_out, d_ff_2_q);
  D_Flip_Flop d_ff_2 (.D(and_14_out), .clk(Down_out), .Q(d_ff_2_q));  // open: Qn, preset, reset
  and and_15 (and_15_out, counter_7_q[1], counter_7_q[3]);
  and and_16 (and_16_out, counter_7_q[0], counter_7_q[3]);
  Counter #(.max('h7), .trigger("falling"), .width(3)) counter_8 (
    .clr(and_19_out), .up(and_1_out[1]), .count(decoder_2_out3), .clk(multiplexer_15_out), .Q(counter_8_q));  // open: load, D, carry
  and and_17 (and_17_out, not_6_out, nor_8_out);
  Multiplexer #(.select(2)) multiplexer_16 (
    .in0(and_17_out), .in1(and_31_out), .in2(1'b0), .in3(1'b0), .out(multiplexer_16_out),
    .sel({and_1_out[0], and_1_out[1]}));
  _7_Segment_Display u_7_segment_display_9 ();  // open: g, f, a, b, e, d, c, dp
  // BCD_to_7_Segment_decoder bcd_to_7_segment_decoder_9: pin names not known; wires that end beside it: 1'b0
  T_Flip_Flop t_ff_1 (.T(BTNC_out), .clk(counter_4_q[3]), .Q(t_ff_1_q));  // open: Qn, reset, preset
  Multiplexer multiplexer_17 (
    .in0(counter_4_q[3]), .in1(multiplexer_16_out), .out(multiplexer_17_out), .sel(decoder_2_out1));
  Multiplexer multiplexer_18 (.in0(and_22_out), .in1(1'b1), .out(multiplexer_18_out), .sel(decoder_2_out1));
  Comparator #(.width(4)) comparator_2 (.a(counter_7_q), .b(counter_5_q), .eq(comparator_2_eq));  // open: gt, lt
  or or_6 (or_6_out, BTNR_out, BTNL_out);
  and and_18 (and_18_out, Down_out, nor_8_out);
  Counter #(.max('h7), .width(3)) counter_9 (
    .clr(and_26_out), .up(multiplexer_20_out), .count(multiplexer_18_out), .clk(multiplexer_17_out),
    .Q(counter_9_q));  // open: load, D, carry
  and and_19 (and_19_out, counter_8_q[1], counter_8_q[2]);
  // AND_Gate and_20 has open pins: in0=counter_8_q[0], in1=counter_8_q[2], out=open
  and and_21 (and_21_out, nor_6_out, not_4_out);
  and and_22 (and_22_out, and_32_out, and_36_out);
  _7_Segment_Display u_7_segment_display_10 ();  // open: g, f, a, b, e, d, c, dp
  // BCD_to_7_Segment_decoder bcd_to_7_segment_decoder_10: pin names not known; wires that end beside it: 1'b0
  not not_4 (not_4_out, d_ff_3_q);
  not not_5 (not_5_out, t_ff_1_q);
  Multiplexer #(.width(3)) multiplexer_19 (
    .in0(counter_9_q), .in1(counter_8_q), .out(multiplexer_19_out), .sel(bcd_to_7_segment_decoder_2_p3));
  Counter #(.max('h3), .width(2)) counter_10 (
    .clr(not_5_out), .count(t_ff_1_q), .clk(or_6_out), .Q(counter_10_q));  // open: load, up, D, carry
  not not_6 (not_6_out, d_ff_4_q);
  and and_23 (and_23_out, counter_9_q[0], counter_9_q[2]);
  and and_24 (and_24_out, and_23_out, and_36_out, and_32_out);
  and and_25 (and_25_out, nor_6_out, Down_out);
  and and_26 (and_26_out, counter_9_q[1], counter_9_q[2]);
  Counter #(.max('hf), .width(4)) counter_11 (
    .clr(and_29_out), .load(and_25_out), .up(and_1_out[1]), .count(decoder_2_out3), .clk(or_1_out), .D(in_3),
    .Q(counter_11_q));  // open: carry
  Multiplexer multiplexer_20 (.in0(1'b1), .in1(and_1_out[1]), .out(multiplexer_20_out), .sel(decoder_2_out1));
  _7_Segment_Display u_7_segment_display_11 ();  // open: g, f, a, b, e, d, c, dp
  // BCD_to_7_Segment_decoder bcd_to_7_segment_decoder_11: pin names not known; wires that end beside it: counter_11_q
  Multiplexer multiplexer_21 (.in0(counter_4_q[3]), .in1(or_1_out), .out(multiplexer_21_out), .sel(decoder_2_out1));
  Multiplexer multiplexer_22 (.in0(and_36_out), .in1(1'b1), .out(multiplexer_22_out), .sel(decoder_2_out1));
  Counter #(.max('hf), .width(4)) counter_12 (
    .clr(and_31_out), .load(and_18_out), .up(multiplexer_20_out), .count(multiplexer_22_out),
    .clk(multiplexer_21_out), .D(in_2), .Q(counter_12_q));  // open: carry
  and and_27 (and_27_out, counter_11_q[0], nor_7_out);
  nor nor_6 (nor_6_out, counter_11_q[3], counter_11_q[0], counter_11_q[1], counter_11_q[2]);
  Decoder #(.select(2)) decoder_2 (
    .out0(decoder_2_out0), .out1(decoder_2_out1), .out2(decoder_2_out2), .out3(decoder_2_out3),
    .sel(counter_10_q));  // open: en
  and and_28 (and_28_out, t_ff_1_q, decoder_2_out0);
  _7_Segment_Display u_7_segment_display_12 ();  // open: g, f, a, b, e, d, c, dp
  // BCD_to_7_Segment_decoder bcd_to_7_segment_decoder_12: pin names not known; wires that end beside it: bcd_to_7_segment_decoder_12_p1, counter_12_q
  D_Flip_Flop d_ff_3 (.D(and_27_out), .clk(Down_out), .Q(d_ff_3_q));  // open: Qn, preset, reset
  nor nor_7 (nor_7_out, counter_11_q[1], counter_11_q[2], counter_11_q[3]);
  Comparator #(.width(3)) comparator_3 (.a(counter_9_q), .b(counter_8_q), .eq(comparator_3_eq));  // open: gt, lt
  and and_29 (and_29_out, counter_11_q[1], counter_11_q[3]);
  and and_30 (and_30_out, counter_12_q[0], nor_9_out);
  nor nor_8 (nor_8_out, counter_12_q[3], counter_12_q[2], counter_12_q[1], counter_12_q[0]);
  Multiplexer #(.width(4)) multiplexer_23 (
    .in0(counter_12_q), .in1(counter_11_q), .out(bcd_to_7_segment_decoder_12_p1),
    .sel(bcd_to_7_segment_decoder_2_p3));
  D_Flip_Flop d_ff_4 (.D(and_30_out), .clk(Down_out), .Q(d_ff_4_q));  // open: Qn, preset, reset
  nor nor_9 (nor_9_out, counter_12_q[1], counter_12_q[2], counter_12_q[3]);
  and and_31 (and_31_out, counter_12_q[1], counter_12_q[3]);
  and and_32 (and_32_out, counter_12_q[0], counter_12_q[3]);
  Comparator #(.width(4)) comparator_4 (.a(counter_12_q), .b(counter_11_q), .eq(comparator_4_eq));  // open: gt, lt
  Multiplexer multiplexer_24 (.in0(and_35_out), .in1(1'b1), .out(multiplexer_24_out), .sel(t_ff_1_q));
  Counter #(.max('h3f), .width(6)) counter_13 (
    .clr(multiplexer_24_out), .up(1'b1), .count(1'b1), .clk(counter_4_q[3]), .Q(counter_13_q));  // open: load, D, carry
  and and_33 (and_33_out, comparator_1_eq, comparator_2_eq, comparator_4_eq, comparator_3_eq);
  and and_34 (and_34_out, and_33_out, not_7_out);
  or or_7 (bcd_to_7_segment_decoder_2_p3, decoder_2_out2, decoder_2_out3);
  T_Flip_Flop t_ff_2 (.T(and_34_out), .clk(counter_4_q[3]), .Q(t_ff_2_q));  // open: Qn, reset, preset
  and and_35 (and_35_out, counter_13_q[2], counter_13_q[3], counter_13_q[4], counter_13_q[5]);
  and and_36 (and_36_out, counter_13_q[0], counter_13_q[1], counter_13_q[3], counter_13_q[4], counter_13_q[5]);
  not not_7 (not_7_out, BTNC_out);
  LED led_1 (.in(t_ff_2_q));

  // Notes on the sheet:
  //   in_4: initial=0x9
  //   in_1: initial=0x9
  //   in_3: initial=0x9
  //   in_2: initial=0x9
  //   nor
  //   and
  //   or
  //   down
  //   Clock Divider
  //   `
  //   clk 1HZ
  //   0 : State Clock / 1 : TIme Hours
  //   State Time Minutes
  //   alarm minutes
  //   CU
endmodule
